// Logisim project circuito.circ as structural Verilog
module main (
);

  BC bc_1 ();
  BO bo_1 ();  // open: A, B, C, X, M0, LX, clk, M2, M1, H, LS, LH, resultado
endmodule

module BO (
  input  [15:0] A,
  input  [15:0] B,
  input  [15:0] C,
  input  [15:0] X,
  input  [1:0] M0,
  input  LX,
  input  clk,
  input  [1:0] M2,
  input  [1:0] M1,
  input  H,
  input  LS,
  input  LH,
  output [15:0] resultado
);

  wire [15:0] multiplexer_1_out, multiplexer_2_out, multiplexer_3_out, register_1_q, register_3_q,
       somadormultiplicador_1_saida;

  Register #(.width(16)) register_1 (.D(X), .en(LX), .clk(clk), .Q(register_1_q));  // open: clr
  Register #(.width(16)) register_2 (.D(somadormultiplicador_1_saida), .en(LS), .clk(clk), .Q(resultado));  // open: clr
  Multiplexer #(.select(2), .width(16)) multiplexer_1 (
    .in0(register_1_q), .in1(multiplexer_2_out), .in2(resultado), .in3(register_3_q),
    .out(multiplexer_1_out), .sel(M2));
  SomadorMultiplicador somadormultiplicador_1 (
    .a(multiplexer_3_out), .b(multiplexer_1_out), .entrada(H), .saida(somadormultiplicador_1_saida));
  Register #(.width(16)) register_3 (
    .D(somadormultiplicador_1_saida), .en(LH), .clk(clk), .Q(register_3_q));  // open: clr
  Multiplexer #(.select(2), .width(16)) multiplexer_2 (
    .in1(A), .in2(B), .in3(C), .out(multiplexer_2_out));  // open: in0, sel
  Multiplexer #(.select(2), .width(16)) multiplexer_3 (
    .in0(register_1_q), .in1(multiplexer_2_out), .in2(resultado), .in3(register_3_q),
    .out(multiplexer_3_out), .sel(M1));
endmodule

module SomadorMultiplicador (
  input  [15:0] a,
  input  [15:0] b,
  input  entrada,
  output [15:0] saida
);

  wire [15:0] adder_1_out, multiplier_1_out;

  Adder #(.width(16)) adder_1 (.a(a), .b(b), .out(adder_1_out));  // open: cin, cout
  Multiplier #(.width(16)) multiplier_1 (.a(a), .b(a), .out(multiplier_1_out));  // open: cin, cout
  Multiplexer #(.width(16)) multiplexer_1 (.in0(adder_1_out), .in1(multiplier_1_out), .out(saida), .sel(entrada));
endmodule
